# Fritzing sketch ControlCircuitBoard (saved by Fritzing 1.0.3b)

parts:
  Bauteil3 = INA219 High Side DC Current Sensor Breakout [part_number=904]
  Bauteil4 = INA219 High Side DC Current Sensor Breakout [part_number=904]
  J2 = female pin header, 4 pins [form="♀ (female)"]
  J4 = female pin header, 4 pins [form="♀ (female)"]
  J3 = female pin header, 2 pins [form="♀ (female)"]
  Bauteil5 = Adafruit DC+Stepper FeatherWing [part_number="Adafruit #2927"]

nets:
  VCC: Bauteil3.VCC, Bauteil4.VCC, J2.pin1, Bauteil5.+3.3V
  GND: Bauteil3.GND, Bauteil4.GND, J2.pin2, J3.pin1, Bauteil5.GND
  N1: Bauteil3.SCL, Bauteil4.SCL, Bauteil5.SCL
  N2: Bauteil3.SDA, Bauteil4.SDA, Bauteil5.SDA
  N3: Bauteil3.VIN-, Bauteil5.M1B
  N4: Bauteil3.VIN+, J4.pin1
  N5: Bauteil4.VIN-, Bauteil5.M2B
  N6: Bauteil4.VIN+, J4.pin3
  N7: J2.pin3, Bauteil5.B
  N8: J2.pin4, Bauteil5.C
  N9: J4.pin2, Bauteil5.M1A
  N10: J4.pin4, Bauteil5.M2A
  N11: J3.pin2, Bauteil5.VMOTOR

custom parts:
  INA219 High Side DC Current Sensor Breakout: This breakout board will solve all your power-monitoring problems. Instead of struggling with two multimeters, you can just use the handy INA219B chip on this breakout to both measure both the high side voltage and DC current draw over I2C with 1% precision. Most current-measuring devices such as our current panel meter are only good for low side measuring. That means that unless you want to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
  Adafruit DC+Stepper FeatherWing: This is the DC Motor + Stepper FeatherWing which will let you use 2 x bi-polar stepper motors or 4 x brushed DC motorx (or 1 stepper and 2 DC motors). Using our Feather Stacking Headers or Feather Female Headers you can connect a FeatherWing on top or bottom of your Feather board and let the board take flight! The original Adafruit Motorshield Kit is one of our most beloved kits, which is why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
